// Logisim project regfile.circ as structural Verilog: 1 circuit, main circuit regfile
module regfile (
  input  [4:0] rs1,
  input  [4:0] rs2,
  input  [4:0] rd,
  input  [31:0] Write_Data,
  input  RegWEn,
  input  clk,
  output [31:0] ra,
  output [31:0] sp,
  output [31:0] t0,
  output [31:0] t1,
  output [31:0] t2,
  output [31:0] s0,
  output [31:0] s1,
  output [31:0] a0,
  output [31:0] Read_Data_1,
  output [31:0] Read_Data_2
);

  Register #(.width(32)) register_1 ();  // open: D, en, clk, Q, clr
  Register #(.width(32)) register_2 ();  // open: D, en, clk, Q, clr
  Register #(.width(32)) register_3 ();  // open: D, en, clk, Q, clr
  Register #(.width(32)) register_4 ();  // open: D, en, clk, Q, clr
  Register #(.width(32)) register_5 ();  // open: D, en, clk, Q, clr
  Register #(.width(32)) register_6 ();  // open: D, en, clk, Q, clr
  Register #(.width(32)) register_7 ();  // open: D, en, clk, Q, clr
  Register #(.width(32)) register_8 ();  // open: D, en, clk, Q, clr
  Register #(.width(32)) register_9 ();  // open: D, en, clk, Q, clr
  Register #(.width(32)) register_10 ();  // open: D, en, clk, Q, clr
  Register #(.width(32)) register_11 ();  // open: D, en, clk, Q, clr
  Register #(.width(32)) register_12 ();  // open: D, en, clk, Q, clr
  Register #(.width(32)) register_13 ();  // open: D, en, clk, Q, clr
  Register #(.width(32)) register_14 ();  // open: D, en, clk, Q, clr
  Register #(.width(32)) register_15 ();  // open: D, en, clk, Q, clr
  Register #(.width(32)) register_16 ();  // open: D, en, clk, Q, clr
  Register #(.width(32)) register_17 ();  // open: D, en, clk, Q, clr
  Register #(.width(32)) register_18 ();  // open: D, en, clk, Q, clr
  Register #(.width(32)) register_19 ();  // open: D, en, clk, Q, clr
  Register #(.width(32)) register_20 ();  // open: D, en, clk, Q, clr
  Register #(.width(32)) register_21 ();  // open: D, en, clk, Q, clr
  Register #(.width(32)) register_22 ();  // open: D, en, clk, Q, clr
  Register #(.width(32)) register_23 ();  // open: D, en, clk, Q, clr
  Register #(.width(32)) register_24 ();  // open: D, en, clk, Q, clr
  Register #(.width(32)) register_25 ();  // open: D, en, clk, Q, clr
  Register #(.width(32)) register_26 ();  // open: D, en, clk, Q, clr
  Register #(.width(32)) register_27 ();  // open: D, en, clk, Q, clr
  Register #(.width(32)) register_28 ();  // open: D, en, clk, Q, clr
  Register #(.width(32)) register_29 ();  // open: D, en, clk, Q, clr
  Register #(.width(32)) register_30 ();  // open: D, en, clk, Q, clr
  Register #(.width(32)) register_31 ();  // open: D, en, clk, Q, clr

  // Other names for the same wires on the sheet: read_data1[31:0] = Read_Data_1; read_data2[31:0] = Read_Data_2;
  //   read_reg1[4:0] = rs1; read_reg2[4:0] = rs2; write_en = RegWEn; write_reg[4:0] = rd

  // Notes on the sheet:
  //   INPUTS to your circuit
  //   DON'T CHANGE THE LOCATIONS OF THE INPUTS AND OUTPUTS!
  //   These are DEBUG/TEST outputs from your circuit.
  //   OUTPUTS from your circuit
endmodule
